// Logisim project OurProject.circ as structural Verilog: 3 circuits, main circuit main
module I_O_mapped (
  input  [15:0] add,
  input  data,
  input  clock,
  input  rd_wr,
  input  [7:0] I_Odata,
  output [5:0] out_6,
  output out_7,
  output out_8,
  output out_9,
  output [7:0] out_10
);

  wire nand_1_out;

  nand nand_1 (nand_1_out, add[6], add[7]);
  and and_1 (out_7, nand_1_out, data);
  and and_2 (out_8, data, clock, ~nand_1_out);  // AND_Gate

  assign out_6 = add[5:0];
  assign out_9 = rd_wr;
  assign out_10 = I_Odata;
endmodule

module main (
);

  wire cdm_8_mark5_1_p1, cdm_8_mark5_1_p2, cdm_8_mark5_1_p4, cdm_8_mark5_1_p5, cdm_8_mark5_1_p6,
       cdm_8_mark5_1_p7, cdm_8_mark5_1_p8, cdm_8_mark5_1_p9, CL, code, data, I_Osel, IN_OUT, mem, not_1_out,
       RAM, rd_wr;
  wire [5:0] I_Oaddr;
  wire [7:0] cdm_8_mark5_1_p13, cdm_8_mark5_1_p14, data_out, I_Odata, video_buffer_1_out_6,
       video_buffer_1_out_7, video_buffer_1_out_8, video_buffer_1_out_9, video_buffer_1_out_10,
       video_buffer_1_out_11, video_buffer_1_out_12, video_buffer_1_out_13, video_buffer_1_out_14,
       video_buffer_1_out_15, video_buffer_1_out_16, video_buffer_1_out_17, video_buffer_1_out_18,
       video_buffer_1_out_19, video_buffer_1_out_20, video_buffer_1_out_21, video_buffer_1_out_22,
       video_buffer_1_out_23, video_buffer_1_out_24, video_buffer_1_out_25, video_buffer_1_out_26,
       video_buffer_1_out_27, video_buffer_1_out_28, video_buffer_1_out_29, video_buffer_1_out_31,
       video_buffer_1_out_32, video_buffer_1_out_33, video_buffer_1_out_34, video_buffer_1_out_35,
       video_buffer_1_out_36, video_buffer_1_out_37, video_buffer_1_out_38;
  wire [15:0] cdm_8_mark5_1_p12;

  Clock clock_1 (.out(CL));
  // Probe on cdm_8_mark5_1_p2
  // Probe on cdm_8_mark5_1_p5
  // Probe on cdm_8_mark5_1_p4
  // Probe on cdm_8_mark5_1_p6
  // Probe on cdm_8_mark5_1_p1
  // Probe on cdm_8_mark5_1_p7
  // Probe on cdm_8_mark5_1_p8
  // CdM_8_mark5 cdm_8_mark5_1: pin names not known; wires that end beside it: cdm_8_mark5_1_p1, cdm_8_mark5_1_p2, CL, cdm_8_mark5_1_p4, cdm_8_mark5_1_p5, cdm_8_mark5_1_p6, cdm_8_mark5_1_p7, cdm_8_mark5_1_p8, cdm_8_mark5_1_p9, mem, rd_wr, cdm_8_mark5_1_p12, cdm_8_mark5_1_p13, cdm_8_mark5_1_p14
  assign data_out = not_1_out ? cdm_8_mark5_1_p13 : 8'bz;  // Controlled_Buffer controlled_buffer_1
  not not_1 (not_1_out, rd_wr);
  assign cdm_8_mark5_1_p14 = rd_wr ? data_out : 8'bz;  // Controlled_Buffer controlled_buffer_2
  Decoder #(.disabled(0)) decoder_1 (.out0(code), .out1(data), .sel(cdm_8_mark5_1_p9), .en(mem));
  I_O_mapped i_o_mapped_1 (
    .add(cdm_8_mark5_1_p12), .data(data), .clock(CL), .rd_wr(rd_wr), .I_Odata(data_out), .out_6(I_Oaddr),
    .out_7(RAM), .out_8(I_Osel), .out_9(IN_OUT), .out_10(I_Odata));
  ROM #(.addrWidth(16)) rom_1 (.addr(cdm_8_mark5_1_p12), .data(data_out), .sel(code));
  RAM #(.addrWidth(16)) ram_1 (
    .addr(cdm_8_mark5_1_p12), .data(data_out), .sel(RAM), .clk(CL), .ld(rd_wr));  // open: clr
  video_buffer video_buffer_1 (
    .video_addr(I_Oaddr), .sel(I_Osel), .in_out(IN_OUT), .clock(CL), .data(I_Odata),
    .out_6(video_buffer_1_out_6), .out_7(video_buffer_1_out_7), .out_8(video_buffer_1_out_8),
    .out_9(video_buffer_1_out_9), .out_10(video_buffer_1_out_10), .out_11(video_buffer_1_out_11),
    .out_12(video_buffer_1_out_12), .out_13(video_buffer_1_out_13), .out_14(video_buffer_1_out_14),
    .out_15(video_buffer_1_out_15), .out_16(video_buffer_1_out_16), .out_17(video_buffer_1_out_17),
    .out_18(video_buffer_1_out_18), .out_19(video_buffer_1_out_19), .out_20(video_buffer_1_out_20),
    .out_21(video_buffer_1_out_21), .out_22(video_buffer_1_out_22), .out_23(video_buffer_1_out_23),
    .out_24(video_buffer_1_out_24), .out_25(video_buffer_1_out_25), .out_26(video_buffer_1_out_26),
    .out_27(video_buffer_1_out_27), .out_28(video_buffer_1_out_28), .out_29(video_buffer_1_out_29),
    .data_out(data_out), .out_31(video_buffer_1_out_31), .out_32(video_buffer_1_out_32),
    .out_33(video_buffer_1_out_33), .out_34(video_buffer_1_out_34), .out_35(video_buffer_1_out_35),
    .out_36(video_buffer_1_out_36), .out_37(video_buffer_1_out_37), .out_38(video_buffer_1_out_38));
  DotMatrix #(.inputtype("row"), .matrixcols(8), .matrixrows(32)) dotmatrix_1 (
    .row0(video_buffer_1_out_38), .row1(video_buffer_1_out_37), .row2(video_buffer_1_out_36),
    .row3(video_buffer_1_out_35), .row4(video_buffer_1_out_34), .row5(video_buffer_1_out_33),
    .row6(video_buffer_1_out_32), .row7(video_buffer_1_out_31), .row8(video_buffer_1_out_29),
    .row9(video_buffer_1_out_28), .row10(video_buffer_1_out_27), .row11(video_buffer_1_out_26),
    .row12(video_buffer_1_out_25), .row13(video_buffer_1_out_24), .row14(video_buffer_1_out_23),
    .row15(video_buffer_1_out_22), .row16(video_buffer_1_out_21), .row17(video_buffer_1_out_20),
    .row18(video_buffer_1_out_19), .row19(video_buffer_1_out_18), .row20(video_buffer_1_out_17),
    .row21(video_buffer_1_out_16), .row22(video_buffer_1_out_15), .row23(video_buffer_1_out_14),
    .row24(video_buffer_1_out_13), .row25(video_buffer_1_out_12), .row26(video_buffer_1_out_11),
    .row27(video_buffer_1_out_10), .row28(video_buffer_1_out_9), .row29(video_buffer_1_out_8),
    .row30(video_buffer_1_out_7), .row31(video_buffer_1_out_6));

  // Notes on the sheet:
  //   contents of rom_1 (hex, n*v repeats v):
  //   d0 c0 d1 aa a1 b2 d4
endmodule

module video_buffer (
  input  [5:0] video_addr,
  input  sel,
  input  in_out,
  input  clock,
  input  [7:0] data,
  output [7:0] out_6,
  output [7:0] out_7,
  output [7:0] out_8,
  output [7:0] out_9,
  output [7:0] out_10,
  output [7:0] out_11,
  output [7:0] out_12,
  output [7:0] out_13,
  output [7:0] out_14,
  output [7:0] out_15,
  output [7:0] out_16,
  output [7:0] out_17,
  output [7:0] out_18,
  output [7:0] out_19,
  output [7:0] out_20,
  output [7:0] out_21,
  output [7:0] out_22,
  output [7:0] out_23,
  output [7:0] out_24,
  output [7:0] out_25,
  output [7:0] out_26,
  output [7:0] out_27,
  output [7:0] out_28,
  output [7:0] out_29,
  output [7:0] data_out,
  output [7:0] out_31,
  output [7:0] out_32,
  output [7:0] out_33,
  output [7:0] out_34,
  output [7:0] out_35,
  output [7:0] out_36,
  output [7:0] out_37,
  output [7:0] out_38
);

  wire and_1_out, and_2_out, and_3_out, decoder_1_out0, decoder_1_out1, decoder_1_out2, decoder_1_out3,
       decoder_1_out4, decoder_1_out5, decoder_1_out6, decoder_1_out7, decoder_1_out8, decoder_1_out9,
       decoder_1_out10, decoder_1_out11, decoder_1_out12, decoder_1_out13, decoder_1_out14, decoder_1_out15,
       decoder_1_out16, decoder_1_out17, decoder_1_out18, decoder_1_out19, decoder_1_out20, decoder_1_out21,
       decoder_1_out22, decoder_1_out23, decoder_1_out24, decoder_1_out25, decoder_1_out26, decoder_1_out27,
       decoder_1_out28, decoder_1_out29, decoder_1_out30, decoder_1_out31, video;
  wire [7:0] wrow0, wrow1, wrow2, wrow3, wrow4, wrow5, wrow6, wrow7, wrow8, wrow9, wrow10, wrow11, wrow12,
       wrow13, wrow14, wrow15, wrow16, wrow17, wrow18, wrow19, wrow20, wrow21, wrow22, wrow23, wrow24,
       wrow25, wrow26, wrow27, wrow28, wrow29, wrow30, wrow31;

  not not_1 (video, video_addr[5]);
  and and_1 (and_1_out, ~in_out, sel, video);  // AND_Gate
  Demultiplexer #(.select(5), .width(8), .disabled(0)) demultiplexer_1 (
    .out0(wrow0), .out1(wrow1), .out2(wrow2), .out3(wrow3), .out4(wrow4), .out5(wrow5), .out6(wrow6),
    .out7(wrow7), .out8(wrow8), .out9(wrow9), .out10(wrow10), .out11(wrow11), .out12(wrow12), .out13(wrow13),
    .out14(wrow14), .out15(wrow15), .out16(wrow16), .out17(wrow17), .out18(wrow18), .out19(wrow19),
    .out20(wrow20), .out21(wrow21), .out22(wrow22), .out23(wrow23), .out24(wrow24), .out25(wrow25),
    .out26(wrow26), .out27(wrow27), .out28(wrow28), .out29(wrow29), .out30(wrow30), .out31(wrow31),
    .in(data), .sel(video_addr[4:0]), .en(and_1_out));
  Multiplexer #(.select(5), .width(8)) multiplexer_1 (
    .in0(out_38), .in1(out_37), .in2(out_36), .in3(out_35), .in4(out_34), .in5(out_33), .in6(out_32),
    .in7(out_31), .in8(out_29), .in9(out_28), .in10(out_27), .in11(out_26), .in12(out_25), .in13(out_24),
    .in14(out_23), .in15(out_22), .in16(out_21), .in17(out_20), .in18(out_19), .in19(out_18), .in20(out_17),
    .in21(out_16), .in22(out_15), .in23(out_14), .in24(out_13), .in25(out_12), .in26(out_11), .in27(out_10),
    .in28(out_9), .in29(out_8), .in30(out_7), .in31(out_6), .out(data_out), .sel(video_addr[4:0]),
    .en(and_2_out));
  and and_2 (and_2_out, in_out, video, sel);
  and and_3 (and_3_out, ~in_out, sel, video);  // AND_Gate
  Decoder #(.select(5), .disabled(0)) decoder_1 (
    .out0(decoder_1_out0), .out1(decoder_1_out1), .out2(decoder_1_out2), .out3(decoder_1_out3),
    .out4(decoder_1_out4), .out5(decoder_1_out5), .out6(decoder_1_out6), .out7(decoder_1_out7),
    .out8(decoder_1_out8), .out9(decoder_1_out9), .out10(decoder_1_out10), .out11(decoder_1_out11),
    .out12(decoder_1_out12), .out13(decoder_1_out13), .out14(decoder_1_out14), .out15(decoder_1_out15),
    .out16(decoder_1_out16), .out17(decoder_1_out17), .out18(decoder_1_out18), .out19(decoder_1_out19),
    .out20(decoder_1_out20), .out21(decoder_1_out21), .out22(decoder_1_out22), .out23(decoder_1_out23),
    .out24(decoder_1_out24), .out25(decoder_1_out25), .out26(decoder_1_out26), .out27(decoder_1_out27),
    .out28(decoder_1_out28), .out29(decoder_1_out29), .out30(decoder_1_out30), .out31(decoder_1_out31),
    .sel(video_addr[4:0]), .en(and_3_out));
  Register #(.trigger("falling")) register_1 (.D(wrow15), .en(decoder_1_out15), .Q(out_22), .clk(clock));  // open: clr
  Register #(.trigger("falling")) register_2 (.D(wrow14), .en(decoder_1_out14), .Q(out_23), .clk(clock));  // open: clr
  Register #(.trigger("falling")) register_3 (.D(wrow13), .en(decoder_1_out13), .Q(out_24), .clk(clock));  // open: clr
  Register #(.trigger("falling")) register_4 (.D(wrow12), .en(decoder_1_out12), .Q(out_25), .clk(clock));  // open: clr
  Register #(.trigger("falling")) register_5 (.D(wrow11), .en(decoder_1_out11), .Q(out_26), .clk(clock));  // open: clr
  Register #(.trigger("falling")) register_6 (.D(wrow10), .en(decoder_1_out10), .Q(out_27), .clk(clock));  // open: clr
  Register #(.trigger("falling")) register_7 (.D(wrow9), .en(decoder_1_out9), .Q(out_28), .clk(clock));  // open: clr
  Register #(.trigger("falling")) register_8 (.D(wrow8), .en(decoder_1_out8), .Q(out_29), .clk(clock));  // open: clr
  Register #(.trigger("falling")) register_9 (.D(wrow7), .en(decoder_1_out7), .Q(out_31), .clk(clock));  // open: clr
  Register #(.trigger("falling")) register_10 (.D(wrow6), .en(decoder_1_out6), .Q(out_32), .clk(clock));  // open: clr
  Register #(.trigger("falling")) register_11 (.D(wrow5), .en(decoder_1_out5), .Q(out_33), .clk(clock));  // open: clr
  Register #(.trigger("falling")) register_12 (.D(wrow4), .en(decoder_1_out4), .Q(out_34), .clk(clock));  // open: clr
  Register #(.trigger("falling")) register_13 (.D(wrow3), .en(decoder_1_out3), .Q(out_35), .clk(clock));  // open: clr
  Register #(.trigger("falling")) register_14 (.D(wrow2), .en(decoder_1_out2), .Q(out_36), .clk(clock));  // open: clr
  Register #(.trigger("falling")) register_15 (.D(wrow1), .en(decoder_1_out1), .Q(out_37), .clk(clock));  // open: clr
  Register #(.trigger("falling")) register_16 (.D(wrow0), .en(decoder_1_out0), .Q(out_38), .clk(clock));  // open: clr
  Register #(.trigger("falling")) register_17 (.D(wrow16), .en(decoder_1_out16), .Q(out_21), .clk(clock));  // open: clr
  Register #(.trigger("falling")) register_18 (.D(wrow17), .en(decoder_1_out17), .Q(out_20), .clk(clock));  // open: clr
  Register #(.trigger("falling")) register_19 (.D(wrow18), .en(decoder_1_out18), .Q(out_19), .clk(clock));  // open: clr
  Register #(.trigger("falling")) register_20 (.D(wrow19), .en(decoder_1_out19), .Q(out_18), .clk(clock));  // open: clr
  Register #(.trigger("falling")) register_21 (.D(wrow20), .en(decoder_1_out20), .Q(out_17), .clk(clock));  // open: clr
  Register #(.trigger("falling")) register_22 (.D(wrow21), .en(decoder_1_out21), .Q(out_16), .clk(clock));  // open: clr
  Register #(.trigger("falling")) register_23 (.D(wrow22), .en(decoder_1_out22), .Q(out_15), .clk(clock));  // open: clr
  Register #(.trigger("falling")) register_24 (.D(wrow23), .en(decoder_1_out23), .Q(out_14), .clk(clock));  // open: clr
  Register #(.trigger("falling")) register_25 (.D(wrow24), .en(decoder_1_out24), .Q(out_13), .clk(clock));  // open: clr
  Register #(.trigger("falling")) register_26 (.D(wrow25), .en(decoder_1_out25), .Q(out_12), .clk(clock));  // open: clr
  Register #(.trigger("falling")) register_27 (.D(wrow26), .en(decoder_1_out26), .Q(out_11), .clk(clock));  // open: clr
  Register #(.trigger("falling")) register_28 (.D(wrow27), .en(decoder_1_out27), .Q(out_10), .clk(clock));  // open: clr
  Register #(.trigger("falling")) register_29 (.D(wrow28), .en(decoder_1_out28), .Q(out_9), .clk(clock));  // open: clr
  Register #(.trigger("falling")) register_30 (.D(wrow29), .en(decoder_1_out29), .Q(out_8), .clk(clock));  // open: clr
  Register #(.trigger("falling")) register_31 (.D(wrow30), .en(decoder_1_out30), .Q(out_7), .clk(clock));  // open: clr
  Register #(.trigger("falling")) register_32 (.D(wrow31), .en(decoder_1_out31), .Q(out_6), .clk(clock));  // open: clr

  // Other names for the same wires on the sheet: row0[7:0] = out_38; row1[7:0] = out_37; row2[7:0] = out_36;
  //   row3[7:0] = out_35; row4[7:0] = out_34; row5[7:0] = out_33; row6[7:0] = out_32; row7[7:0] = out_31;
  //   row8[7:0] = out_29; row9[7:0] = out_28; row10[7:0] = out_27; row11[7:0] = out_26; row12[7:0] = out_25;
  //   row13[7:0] = out_24; row14[7:0] = out_23; row15[7:0] = out_22; row16[7:0] = out_21; row17[7:0] = out_20;
  //   row18[7:0] = out_19; row19[7:0] = out_18; row20[7:0] = out_17; row21[7:0] = out_16; row22[7:0] = out_15;
  //   row23[7:0] = out_14; row24[7:0] = out_13; row25[7:0] = out_12; row26[7:0] = out_11; row27[7:0] = out_10;
  //   row28[7:0] = out_9; row29[7:0] = out_8; row30[7:0] = out_7; row31[7:0] = out_6; row_add[4:0] = video_addr[4:0]
endmodule
